// Logisim project taller1.circ as structural Verilog: 17 circuits, main circuit verificador
module sumador_simple (
  input  a,
  input  b,
  output S,
  output Cout
);

  xor xor_1 (S, a, b);
  and and_1 (Cout, a, b);
endmodule

// S_C
module sumador_completo (
  input  Cin,
  input  A,
  input  B,
  output S,
  output Cout
);

  wire sumador_simple_1_cout, sumador_simple_1_s, sumador_simple_2_cout;

  sumador_simple sumador_simple_1 (.a(A), .b(B), .S(sumador_simple_1_s), .Cout(sumador_simple_1_cout));
  sumador_simple sumador_simple_2 (.a(Cin), .b(sumador_simple_1_s), .S(S), .Cout(sumador_simple_2_cout));
  or or_1 (Cout, sumador_simple_2_cout, sumador_simple_1_cout);
endmodule

// sumador
module sumador_4 (
  input  Cin,
  input  [3:0] A,
  input  [3:0] B,
  output [3:0] S,
  output Cout
);

  wire sumador_completo_1_cout, sumador_completo_2_cout, sumador_completo_3_cout;

  sumador_completo sumador_completo_1 (.A(A[0]), .B(B[0]), .Cin(Cin), .S(S[0]), .Cout(sumador_completo_1_cout));
  sumador_completo sumador_completo_2 (
    .A(A[1]), .B(B[1]), .Cin(sumador_completo_1_cout), .S(S[1]), .Cout(sumador_completo_2_cout));
  sumador_completo sumador_completo_3 (
    .A(A[2]), .B(B[2]), .Cin(sumador_completo_2_cout), .S(S[2]), .Cout(sumador_completo_3_cout));
  sumador_completo sumador_completo_4 (.A(A[3]), .B(B[3]), .Cin(sumador_completo_3_cout), .S(S[3]), .Cout(Cout));
  Hex_Digit_Display hex_digit_display_1 (.value(S));  // open: dp
endmodule

module comparador_cero (
  input  [3:0] A,
  output Z
);

  wire not_1_out, not_2_out, not_3_out, not_4_out;

  not not_1 (not_1_out, A[0]);
  not not_2 (not_2_out, A[1]);
  not not_3 (not_3_out, A[2]);
  not not_4 (not_4_out, A[3]);
  and and_1 (Z, not_1_out, not_2_out, not_3_out, not_4_out);
endmodule

// sumador
module sumador_flags (
  input  Cin,
  input  [3:0] A,
  input  [3:0] B,
  output [3:0] S,
  output N,
  output Z,
  output V,
  output C
);

  sumador_4 sumadorFlags (.Cin(Cin), .A(A), .S({N, S[2:0]}), .B(B), .Cout(C));
  overflow overflow (.S({N, S[2:0]}), .A(A), .B(B), .V(V));
  Hex_Digit_Display hex_digit_display_1 (.value({N, S[2:0]}));  // open: dp
  comparador_cero comparadorCero (.A({N, S[2:0]}), .Z(Z));

  assign S[3] = N;
endmodule

module incrementador_4 (
  input  [3:0] A,
  output [3:0] S
);

  sumador_4 sumador_4_1 (.Cin(1'b0), .A(4'b0001), .S(S), .B(A));  // open: Cout
  Hex_Digit_Display hex_digit_display_1 (.value(S));  // open: dp
endmodule

// INV
module inversor_4 (
  input  [3:0] A,
  input  INV,
  output [3:0] S,
  output _1000
);

  wire not_1_out, not_2_out, not_3_out;
  wire [3:0] xor_1_out;

  xor xor_1 (xor_1_out[0], A[0], INV);
  xor xor_2 (xor_1_out[1], A[1], INV);
  xor xor_3 (xor_1_out[2], A[2], INV);
  xor xor_4 (xor_1_out[3], A[3], INV);
  not not_1 (not_1_out, A[0]);
  not not_2 (not_2_out, A[1]);
  not not_3 (not_3_out, A[2]);
  and and_1 (_1000, not_1_out, not_2_out, not_3_out, A[3]);
  sumador_4 sumador_4_1 (.Cin(INV), .A(xor_1_out), .S(S), .B(4'b0000));  // open: Cout
  Hex_Digit_Display hex_digit_display_1 (.value(S));  // open: dp

  // Notes on the sheet:
  //   invierto digitos con xor
  //   agrego +1 como Cin
  //   sumo cero
endmodule

module ALU (
  input  [3:0] A,
  input  [3:0] B,
  input  [1:0] OP,
  output N,
  output Z,
  output V,
  output C,
  output [3:0] S
);

  wire [3:0] A_B_2_n, A_B_2_s, A_B_n, A_B_s, and_1_n, and_1_s, or_1_n, or_1_s;

  sumador_flags A_B (.A(A), .B(B), .Cin(1'b0), .S(A_B_s), .N(A_B_n[0]), .Z(A_B_n[1]), .V(A_B_n[2]), .C(A_B_n[3]));
  OR or_1 (.A(A), .B(B), .S(or_1_s), .N(or_1_n[0]), .Z(or_1_n[1]), .V(or_1_n[2]), .C(or_1_n[3]));
  restador_flags A_B_2 (
    .A(A), .B(B), .Cin(1'b0), .S(A_B_2_s), .N(A_B_2_n[0]), .Z(A_B_2_n[1]), .V(A_B_2_n[2]), .C(A_B_2_n[3]));
  AND and_1 (.A(A), .B(B), .S(and_1_s), .N(and_1_n[0]), .Z(and_1_n[1]), .V(and_1_n[2]), .C(and_1_n[3]));
  Multiplexer #(.select(2), .width(4)) multiplexer_1 (
    .in0(A_B_s), .in1(A_B_2_s), .in2(and_1_s), .in3(or_1_s), .out(S), .sel(OP));  // open: en
  Multiplexer #(.select(2), .width(4)) multiplexer_2 (
    .in0(A_B_n), .in1(A_B_2_n), .in2(and_1_n), .in3(or_1_n), .out({C, V, Z, N}), .sel(OP));  // open: en
  Hex_Digit_Display hex_digit_display_1 (.value(S));  // open: dp
endmodule

module verificador (
  output [3:0] a,
  output [3:0] b,
  output [1:0] Op,
  output N,
  output Z,
  output V,
  output C,
  output [3:0] Res,
  output halt
);

  wire clock_1_out;

  Clock clock_1 (.out(clock_1_out));
  Counter #(.width(10), .max('h3ff)) counter_1 (
    .Q({Op, b, a}), .carry(halt), .clk(clock_1_out));  // open: load, D, count, clr
  ALU alu_1 (.A(a), .B(b), .OP(Op), .N(N), .Z(Z), .V(V), .C(C), .S(Res));
  sumador_simple sumador_simple_1 ();  // open: a, b, S, Cout
endmodule

module overflow (
  input  [3:0] S,
  input  [3:0] A,
  input  [3:0] B,
  output V
);

  wire not_1_out, xor_1_out, xor_2_out;

  xor xor_1 (xor_1_out, A[3], B[3]);
  xor xor_2 (xor_2_out, S[3], A[3]);
  not not_1 (not_1_out, xor_1_out);
  and and_1 (V, xor_2_out, not_1_out);

  // Notes on the sheet:
  //   hay problema con el overflow, eliminar casos puntuales del restador
  //   iguales A3 y B3?
  //   diferentes A3 y S3?
endmodule

module AND (
  input  [3:0] A,
  input  [3:0] B,
  output [3:0] S,
  output N,
  output Z,
  output V,
  output C
);

  assign {N, S[2:0]} = A & B;  // AND_Gate and_1, 4 bits wide
  comparador_cero esCero (.A({N, S[2:0]}), .Z(Z));

  assign C = 1'b0;
  assign S[3] = N;
  assign V = 1'b0;
endmodule

module OR (
  input  [3:0] A,
  input  [3:0] B,
  output [3:0] S,
  output N,
  output Z,
  output V,
  output C
);

  assign {N, S[2:0]} = A | B;  // OR_Gate or_1, 4 bits wide
  comparador_cero esCero (.A({N, S[2:0]}), .Z(Z));

  assign C = 1'b0;
  assign S[3] = N;
  assign V = 1'b0;
endmodule

module borrow_simple (
  input  a,
  input  b,
  output borrow
);

  wire not_1_out;

  not not_1 (not_1_out, a);
  and and_1 (borrow, not_1_out, b);
endmodule

module borrow_flags (
  input  [3:0] A,
  input  [3:0] B,
  output Borrow
);

  wire borrow_borrow, restador_2_borrow, restador_borrow;

  borrow_simple u_borrow (.a(A[0]), .b(B[0]), .borrow(borrow_borrow));
  pseudo_restador restador (.a(A[1]), .b(B[1]), .mePidieron(borrow_borrow), .Borrow(restador_borrow));
  pseudo_restador restador_2 (.a(A[2]), .b(B[2]), .mePidieron(restador_borrow), .Borrow(restador_2_borrow));
  pseudo_restador restador_3 (.a(A[3]), .b(B[3]), .mePidieron(restador_2_borrow), .Borrow(Borrow));
endmodule

module pseudo_restador (
  input  mePidieron,
  input  a,
  input  b,
  output Borrow
);

  wire and_1_out, and_2_out, and_3_out, not_1_out, not_2_out, not_3_out, not_4_out, not_5_out, or_1_out;

  not not_1 (not_1_out, mePidieron);
  and and_1 (and_1_out, not_1_out, a);
  not not_2 (not_2_out, mePidieron);
  and and_2 (and_2_out, not_2_out, not_3_out, not_4_out);
  not not_3 (not_3_out, a);
  not not_4 (not_4_out, b);
  and and_3 (and_3_out, a, not_5_out);
  not not_5 (not_5_out, b);
  or or_1 (or_1_out, and_1_out, and_2_out, and_3_out);
  not not_6 (Borrow, or_1_out);
endmodule

// restador
module restador_flags (
  input  Cin,
  input  [3:0] A,
  input  [3:0] B,
  output [3:0] S,
  output N,
  output Z,
  output V,
  output C
);

  wire inversor_4_1__1000, overflow_v;
  wire [3:0] inversor_4_1_s;

  inversor_4 inversor_4_1 (.A(B), .S(inversor_4_1_s), .INV(1'b1), ._1000(inversor_4_1__1000));
  borrow_flags borrow (.A(A), .B(B), .Borrow(C));
  sumador_4 sumadorFlags (.Cin(Cin), .A(A), .S({N, S[2:0]}), .B(inversor_4_1_s));  // open: Cout
  overflow overflow (.S({N, S[2:0]}), .A(A), .B(inversor_4_1_s), .V(overflow_v));
  Hex_Digit_Display hex_digit_display_1 (.value({N, S[2:0]}));  // open: dp
  comparador_cero comparadorCero (.A({N, S[2:0]}), .Z(Z));
  caso_1000 caso1000 (.O(overflow_v), ._1000(inversor_4_1__1000), .A(A), .O_2(V));

  assign S[3] = N;
endmodule

module caso_1000 (
  input  O,
  input  _1000,
  input  [3:0] A,
  output O_2
);

  wire and_1_out, and_2_out, nor_1_out, not_1_out, not_2_out;

  and and_1 (and_1_out, _1000, A[3]);
  not not_1 (not_1_out, O);
  and and_2 (and_2_out, not_1_out, A[3], not_2_out);
  not not_2 (not_2_out, _1000);
  nor nor_1 (nor_1_out, O, _1000, A[3]);
  nor nor_2 (O_2, and_2_out, nor_1_out, and_1_out);
endmodule
