// Logisim project TallerLogica-Secuenciales.circ as structural Verilog: 8 circuits, main circuit 3estados
module _3estados (
  input  A,
  input  A_en,
  input  B,
  input  B_en,
  input  C,
  input  C_en,
  output Res
);

  assign Res = A_en ? A : 1'bz;  // Controlled_Buffer controlled_buffer_1
  assign Res = B_en ? B : 1'bz;  // Controlled_Buffer controlled_buffer_2
  assign Res = C_en ? C : 1'bz;  // Controlled_Buffer controlled_buffer_3

  // Notes on the sheet:
  //   Ejercicio 1
endmodule

module ej_2 (
  input  W_0,
  input  en_0,
  input  W_1,
  input  en_1,
  input  clk,
  input  W_2,
  input  en_2,
  input  Force_input,
  input  en_force_input,
  output R0,
  output BUS,
  output R1,
  output R2
);

  assign BUS = en_force_input ? Force_input : 1'bz;  // Controlled_Buffer controlled_buffer_1
  registro_salida_restringida registro_salida_restringida_1 (
    .clk(clk), .in(BUS), .out_debug(R0), .out(BUS), .w(W_0), .en_out(en_0));
  registro_salida_restringida registro_salida_restringida_2 (
    .clk(clk), .in(BUS), .out_debug(R1), .out(BUS), .w(W_1), .en_out(en_1));
  registro_salida_restringida registro_salida_restringida_3 (
    .clk(clk), .in(BUS), .out_debug(R2), .out(BUS), .w(W_2), .en_out(en_2));

  // Notes on the sheet:
  //   Ejercicio 2
endmodule

module registro_salida_restringida (
  input  clk,
  input  in,
  input  w,
  input  en_out,
  output out_debug,
  output out
);

  wire and_1_out;

  and and_1 (and_1_out, clk, w);
  ffD ffD (.D(in), .clk(and_1_out), .Q(out_debug));  // open: Q_prime
  assign out = en_out ? out_debug : 1'bz;  // Controlled_Buffer controlled_buffer_1

  // Notes on the sheet:
  //   Registro 1b salida restringida
endmodule

module ej_3 (
  input  clk,
  input  w_alu_A,
  input  w_alu_B,
  input  [1:0] op,
  input  en_out_ALU,
  input  W_0,
  input  en_out_0,
  input  W_1,
  input  en_out_1,
  input  W_2,
  input  en_out_2,
  input  W_3,
  input  en_out_3,
  input  [3:0] Force_input,
  input  en_force_input,
  output N,
  output Z,
  output V,
  output C
);

  wire [3:0] alu_con_reg_1_a_debug, alu_con_reg_1_b_debug, alu_con_reg_1_s_debug, controlled_buffer_1_out,
       registro_4b_salida_restringida_1_out, registro_4b_salida_restringida_1_out4_d,
       registro_4b_salida_restringida_2_out4_d, registro_4b_salida_restringida_3_out4_d,
       registro_4b_salida_restringida_4_out4_d;

  registro_4b_salida_restringida registro_4b_salida_restringida_1 (
    .In_4(controlled_buffer_1_out), .clk(clk), .w(W_0), .en_out(en_out_0),
    .out4_d(registro_4b_salida_restringida_1_out4_d), .out(registro_4b_salida_restringida_1_out));
  registro_4b_salida_restringida registro_4b_salida_restringida_2 (
    .In_4(controlled_buffer_1_out), .clk(clk), .w(W_1), .en_out(en_out_1),
    .out4_d(registro_4b_salida_restringida_2_out4_d), .out(registro_4b_salida_restringida_1_out));
  registro_4b_salida_restringida registro_4b_salida_restringida_3 (
    .In_4(controlled_buffer_1_out), .clk(clk), .w(W_2), .en_out(en_out_2),
    .out4_d(registro_4b_salida_restringida_3_out4_d), .out(registro_4b_salida_restringida_1_out));
  registro_4b_salida_restringida registro_4b_salida_restringida_4 (
    .In_4(controlled_buffer_1_out), .clk(clk), .w(W_3), .en_out(en_out_3),
    .out4_d(registro_4b_salida_restringida_4_out4_d), .out(registro_4b_salida_restringida_1_out));
  assign controlled_buffer_1_out = en_force_input ? Force_input : 4'bz;  // Controlled_Buffer controlled_buffer_1
  Hex_Digit_Display hex_digit_display_1 (.value(registro_4b_salida_restringida_1_out4_d));  // open: dp
  Hex_Digit_Display hex_digit_display_2 (.value(registro_4b_salida_restringida_2_out4_d));  // open: dp
  Hex_Digit_Display hex_digit_display_3 (.value(registro_4b_salida_restringida_3_out4_d));  // open: dp
  Hex_Digit_Display hex_digit_display_4 (.value(registro_4b_salida_restringida_4_out4_d));  // open: dp
  Hex_Digit_Display hex_digit_display_5 (.value(registro_4b_salida_restringida_1_out));  // open: dp
  Hex_Digit_Display hex_digit_display_6 (.value(alu_con_reg_1_a_debug));  // open: dp
  Hex_Digit_Display hex_digit_display_7 (.value(alu_con_reg_1_b_debug));  // open: dp
  Hex_Digit_Display hex_digit_display_8 (.value(alu_con_reg_1_s_debug));  // open: dp
  ALU_con_Reg alu_con_reg_1 (
    .clk(clk), .A(registro_4b_salida_restringida_1_out), .Write_A(w_alu_A),
    .B(registro_4b_salida_restringida_1_out), .Write_B(w_alu_B), .OP(op), .A_debug(alu_con_reg_1_a_debug),
    .B_debug(alu_con_reg_1_b_debug), .S_debug(alu_con_reg_1_s_debug), .en_out(en_out_ALU), .N(N), .Z(Z),
    .V(V), .C(C), .S(controlled_buffer_1_out));
  Hex_Digit_Display hex_digit_display_9 (.value(controlled_buffer_1_out));  // open: dp

  // Notes on the sheet:
  //   Ejercicio 3
  //   Bus 1
  //   op
  //   =
  //   Bus 2
endmodule

module registro_4b_salida_restringida (
  input  [3:0] In_4,
  input  clk,
  input  w,
  input  en_out,
  output [3:0] out4_d,
  output [3:0] out
);

  registro_salida_restringida registro_salida_restringida_1 (
    .clk(clk), .in(In_4[0]), .out_debug(out4_d[0]), .out(out[0]), .w(w), .en_out(en_out));
  registro_salida_restringida registro_salida_restringida_2 (
    .clk(clk), .in(In_4[1]), .out_debug(out4_d[1]), .out(out[1]), .w(w), .en_out(en_out));
  registro_salida_restringida registro_salida_restringida_3 (
    .clk(clk), .in(In_4[2]), .out_debug(out4_d[2]), .out(out[2]), .w(w), .en_out(en_out));
  registro_salida_restringida registro_salida_restringida_4 (
    .clk(clk), .in(In_4[3]), .out_debug(out4_d[3]), .out(out[3]), .w(w), .en_out(en_out));

  // Notes on the sheet:
  //   Registro 4b salida restringida
endmodule

module ALU_con_Reg (
  input  clk,
  input  [3:0] A,
  input  Write_A,
  input  [3:0] B,
  input  Write_B,
  input  [1:0] OP,
  input  en_out,
  output [3:0] A_debug,
  output [3:0] B_debug,
  output N,
  output Z,
  output V,
  output C,
  output [3:0] S_debug,
  output [3:0] S
);

  wire not_1_out;
  wire [3:0] ALU_s, registro_4b_salida_restringida_1_out, registro_4b_salida_restringida_2_out;

  Hex_Digit_Display hex_digit_display_1 (.value(A_debug));  // open: dp
  registro_4b_salida_restringida registro_4b_salida_restringida_1 (
    .In_4(A), .clk(clk), .w(Write_A), .en_out(1'b1), .out4_d(A_debug),
    .out(registro_4b_salida_restringida_1_out));
  registro_4b_salida_restringida registro_4b_salida_restringida_2 (
    .In_4(B), .clk(clk), .w(Write_B), .en_out(1'b1), .out4_d(B_debug),
    .out(registro_4b_salida_restringida_2_out));
  Hex_Digit_Display hex_digit_display_2 (.value(B_debug));  // open: dp
  ALU ALU (
    .A(registro_4b_salida_restringida_1_out), .B(registro_4b_salida_restringida_2_out), .OP(OP), .N(N),
    .Z(Z), .V(V), .C(C), .S(ALU_s));
  not not_1 (not_1_out, clk);
  registro_4b_salida_restringida registro_4b_salida_restringida_3 (
    .In_4(ALU_s), .clk(not_1_out), .w(1'b1), .en_out(en_out), .out4_d(S_debug), .out(S));
  Hex_Digit_Display hex_digit_display_3 (.value(S_debug));  // open: dp
endmodule

module ffSR (
  input  R,
  input  clk,
  input  S,
  output Q,
  output Q_prime
);

  wire and_1_out, and_2_out;

  and and_1 (and_1_out, R, clk);
  and and_2 (and_2_out, clk, S);
  nor nor_1 (Q, and_1_out, Q_prime);
  nor nor_2 (Q_prime, Q, and_2_out);
endmodule

module ffD (
  input  D,
  input  clk,
  output Q,
  output Q_prime
);

  wire not_1_out;

  not not_1 (not_1_out, D);
  ffSR ffSR (.R(not_1_out), .clk(clk), .S(D), .Q(Q), .Q_prime(Q_prime));
endmodule
